# Fritzing sketch door-sensor-alarm (saved by Fritzing 0.9.3b)
breadboards: 1

parts:
  R1 = Resistor [tolerance=±5% resistance=220 package="2512 [SMD]"]
  LED1 = LED - 5mm [color="Red (633nm)" package="5 mm [THT]"]
  Part1 = Photon
  S1 = Reed switch [package=THT]
  J1 = Piezo Speaker

nets:
  N1: R1.Pin_0, LED1.cathode
  N2: R1.Pin_1, Part1.GND, S1.pin_2, J1.pin1
  N3: LED1.anode, Part1.D0
  N4: Part1.D1, J1.pin2
  N5: Part1.D3, S1.pin_1
